// Logisim project ProcessorDesign.circ as structural Verilog: 4 circuits, main circuit main
module main (
  input  in_1,
  input  in_2,
  output [3:0] bp,
  output [3:0] sp,
  output [3:0] t5,
  output [3:0] t4,
  output [3:0] t3,
  output [3:0] t2,
  output [3:0] t1,
  output [3:0] t0
);

  wire and_2_out, clock_1_out, control_unit_1_alusrc, control_unit_1_branch, control_unit_1_jump,
       control_unit_1_memread, control_unit_1_memwrite, control_unit_1_regdst, control_unit_1_regwrite,
       mips_alu_4_bit_1_p4;
  wire [2:0] InsSplitter_rd_2_0, InsSplitter_rs_11_8, InsSplitter_rt_7_4, multiplexer_1_out;
  wire [3:0] adder_1_p3, and_1_out, control_unit_1_alu_control, incrementer_1_p2, InsSplitter_const_3_0,
       InsSplitter_op_15_12, mips_alu_4_bit_1_p5, multiplexer_2_out, multiplexer_3_out, multiplexer_4_out,
       multiplexer_5_out, PC_q, ram_2_data, registerfile_1_data1, registerfile_1_data2;
  wire [15:0] ram_1_data;

  Register #(.width(4)) PC (.D(multiplexer_4_out), .Q(PC_q), .clk(clock_1_out), .clr(in_2));  // open: en
  // Incrementer incrementer_1: pin names not known; wires that end beside it: PC_q, incrementer_1_p2
  Control_Unit control_unit_1 (
    .OpIn(InsSplitter_op_15_12), .ALU_Control(control_unit_1_alu_control),
    .RegWrite(control_unit_1_regwrite), .RegDst(control_unit_1_regdst), .ALUSrc(control_unit_1_alusrc),
    .Branch(control_unit_1_branch), .MemRead(control_unit_1_memread), .MemWrite(control_unit_1_memwrite),
    .jump(control_unit_1_jump));  // open: reset
  InstructionSplitter InsSplitter (
    .instruction_in(ram_1_data), .OP_15_12(InsSplitter_op_15_12), .rs_11_8(InsSplitter_rs_11_8),
    .rt_7_4(InsSplitter_rt_7_4), .rd_2_0(InsSplitter_rd_2_0), .const_3_0(InsSplitter_const_3_0));
  RAM #(.addrWidth(4), .dataWidth(16)) ram_1 (
    .addr(PC_q), .data(ram_1_data), .clk(clock_1_out), .clr(in_1));  // open: sel, ld
  Multiplexer #(.width(3), .enable("false")) multiplexer_1 (
    .in0(InsSplitter_rt_7_4), .in1(InsSplitter_rd_2_0), .out(multiplexer_1_out), .sel(control_unit_1_regdst));
  assign and_1_out = incrementer_1_p2 & InsSplitter_const_3_0;  // AND_Gate and_1, 4 bits wide
  RegisterFile registerfile_1 (
    .REG1(InsSplitter_rs_11_8), .REG2(InsSplitter_rt_7_4), .Write_REG(multiplexer_1_out),
    .Write_Data(multiplexer_5_out), .WE(control_unit_1_regwrite), .CLK(clock_1_out), .Clear(in_1),
    .Data({bp, sp, t5, t4, t3, t2, t1, t0}), .Data1(registerfile_1_data1), .Data2(registerfile_1_data2));
  Multiplexer #(.width(4), .enable("false")) multiplexer_2 (
    .in0(registerfile_1_data2), .in1(InsSplitter_const_3_0), .out(multiplexer_2_out),
    .sel(control_unit_1_alusrc));
  // Adder adder_1: pin names not known; wires that end beside it: incrementer_1_p2, InsSplitter_const_3_0, adder_1_p3
  // MIPS_ALU_4_bit mips_alu_4_bit_1: pin names not known; wires that end beside it: registerfile_1_data1, multiplexer_2_out, control_unit_1_alu_control, mips_alu_4_bit_1_p4, mips_alu_4_bit_1_p5
  and and_2 (and_2_out, control_unit_1_branch, mips_alu_4_bit_1_p4);
  Multiplexer #(.width(4), .enable("false")) multiplexer_3 (
    .in0(incrementer_1_p2), .in1(adder_1_p3), .out(multiplexer_3_out), .sel(and_2_out));
  Multiplexer #(.width(4), .enable("false")) multiplexer_4 (
    .in0(multiplexer_3_out), .in1(and_1_out), .out(multiplexer_4_out), .sel(control_unit_1_jump));
  RAM #(.addrWidth(4), .dataWidth(4), .bus("separate")) ram_2 (
    .addr(mips_alu_4_bit_1_p5), .din(registerfile_1_data2), .data(ram_2_data), .str(control_unit_1_memwrite),
    .sel(1'b1), .clk(clock_1_out), .ld(control_unit_1_memread), .clr(in_1));
  Multiplexer #(.width(4), .enable("false")) multiplexer_5 (
    .in0(mips_alu_4_bit_1_p5), .in1(ram_2_data), .out(multiplexer_5_out), .sel(control_unit_1_memread));
  Clock clock_1 (.out(clock_1_out));

  // Notes on the sheet:
  //   Instruction memory
  //   ALU
endmodule

module InstructionSplitter (
  input  [15:0] instruction_in,
  output [3:0] OP_15_12,
  output [2:0] rs_11_8,
  output [2:0] rt_7_4,
  output [2:0] rd_2_0,
  output [3:0] const_3_0
);


  assign const_3_0 = instruction_in[3:0];
  assign OP_15_12 = instruction_in[15:12];
  assign rd_2_0 = instruction_in[2:0];
  assign rs_11_8 = instruction_in[10:8];
  assign rt_7_4 = instruction_in[6:4];
endmodule

module RegisterFile (
  input  WE,
  input  [2:0] REG1,
  input  [2:0] REG2,
  input  [2:0] Write_REG,
  input  [3:0] Write_Data,
  input  Clear,
  input  CLK,
  output [3:0] Data1,
  output [3:0] Data2,
  output [31:0] Data
);

  wire and_1_out, and_2_out, and_3_out, and_4_out, and_5_out, and_6_out, and_7_out, decoder_1_out0,
       decoder_1_out1, decoder_1_out2, decoder_1_out3, decoder_1_out4, decoder_1_out5, decoder_1_out6,
       decoder_1_out7;

  Decoder #(.select(3), .enable("false")) decoder_1 (
    .out0(decoder_1_out0), .out1(decoder_1_out1), .out2(decoder_1_out2), .out3(decoder_1_out3),
    .out4(decoder_1_out4), .out5(decoder_1_out5), .out6(decoder_1_out6), .out7(decoder_1_out7),
    .sel(Write_REG));
  and and_1 (and_1_out, WE, decoder_1_out0);
  and and_2 (and_2_out, WE, decoder_1_out1);
  and and_3 (and_3_out, WE, decoder_1_out2);
  and and_4 (and_4_out, WE, decoder_1_out3);
  and and_5 (and_5_out, WE, decoder_1_out4);
  and and_6 (and_6_out, WE, decoder_1_out5);
  and and_7 (and_7_out, WE, decoder_1_out6);
  Register #(.width(4)) t0 (.D(Write_Data), .en(and_1_out), .Q(Data[3:0]), .clk(CLK), .clr(Clear));
  Register #(.width(4)) t1 (.D(Write_Data), .en(and_2_out), .Q(Data[7:4]), .clk(CLK), .clr(Clear));
  Register #(.width(4)) t2 (.D(Write_Data), .en(and_3_out), .Q(Data[11:8]), .clk(CLK), .clr(Clear));
  Register #(.width(4)) t3 (.D(Write_Data), .en(and_4_out), .Q(Data[15:12]), .clk(CLK), .clr(Clear));
  Register #(.width(4)) t4 (.D(Write_Data), .en(and_5_out), .Q(Data[19:16]), .clk(CLK), .clr(Clear));
  Register #(.width(4)) t5 (.D(Write_Data), .en(and_6_out), .Q(Data[23:20]), .clk(CLK), .clr(Clear));
  Register #(.width(4)) sp (.D(Write_Data), .en(and_7_out), .Q(Data[27:24]), .clk(CLK), .clr(Clear));
  Register #(.width(4)) bp (.D(4'b0000), .Q(Data[31:28]), .clk(CLK), .clr(Clear));  // open: en
  Multiplexer #(.select(3), .width(4), .enable("false")) multiplexer_1 (
    .in0(Data[3:0]), .in1(Data[7:4]), .in2(Data[11:8]), .in3(Data[15:12]), .in4(Data[19:16]),
    .in5(Data[23:20]), .in6(Data[27:24]), .in7(Data[31:28]), .out(Data1), .sel(REG1));
  Multiplexer #(.select(3), .width(4), .enable("false")) multiplexer_2 (
    .in0(Data[3:0]), .in1(Data[7:4]), .in2(Data[11:8]), .in3(Data[15:12]), .in4(Data[19:16]),
    .in5(Data[23:20]), .in6(Data[27:24]), .in7(Data[31:28]), .out(Data2), .sel(REG2));
endmodule

module Control_Unit (
  input  [3:0] OpIn,
  output [3:0] ALU_Control,
  output RegWrite,
  output RegDst,
  output ALUSrc,
  output reset,
  output Branch,
  output MemRead,
  output MemWrite,
  output jump
);

  wire decoder_1_out1, decoder_1_out2, decoder_1_out3, decoder_1_out6, decoder_1_out7, decoder_1_out8,
       decoder_1_out9, decoder_1_out12;

  Decoder #(.select(4), .enable("false")) decoder_1 (
    .out0(reset), .out1(decoder_1_out1), .out2(decoder_1_out2), .out3(decoder_1_out3), .out4(MemRead),
    .out5(MemWrite), .out6(decoder_1_out6), .out7(decoder_1_out7), .out8(decoder_1_out8),
    .out9(decoder_1_out9), .out10(Branch), .out11(jump), .out12(decoder_1_out12), .sel(OpIn));  // open: out13, out14, out15
  ROM #(.addrWidth(4), .dataWidth(4)) rom_1 (.addr(OpIn), .data(ALU_Control));  // open: sel
  or Reg_Dest (RegDst, decoder_1_out2, decoder_1_out7, decoder_1_out9, decoder_1_out12);
  or u_ALUSrc (ALUSrc, decoder_1_out8, decoder_1_out6, MemWrite, MemRead, decoder_1_out3, decoder_1_out1);
  or WE (RegWrite, decoder_1_out1, decoder_1_out2, decoder_1_out3, MemRead, decoder_1_out6, decoder_1_out7, decoder_1_out8, decoder_1_out9, decoder_1_out12);

  // Notes on the sheet:
  //   contents of rom_1 (hex, n*v repeats v):
  //   0 0 1 1 4*2 6 0 6 0 6
endmodule
